// Logisim project FinalProject.circ as structural Verilog: 8 circuits, main circuit main
module main (
  input  Manual_cycle,
  input  Reset
);

  wire bus_control_1_alu_enable, bus_control_1_ram_read, bus_control_1_ram_write,
       bus_control_1_register_write, Goto_enable;
  wire [1:0] clock_1_state;
  wire [3:0] A, B, bus_control_1_opcode_to_alu, D, decoder_1_opcode, imm1, imm2, imm3;
  wire [7:0] goto_imm, Instruction, multiplexer_1_out;
  wire [15:0] rom_1_data;
  wire [31:0] alu_1_output, n16_register_file_1_a, n16_register_file_1_b;

  decoder decoder_1 (
    .Input(rom_1_data), .RegB(B), .RegA(A), .Destination_register(D), .opcode(decoder_1_opcode), .Imm3(imm3),
    .Imm2(imm2), .Imm1(imm1), .GoTo_Imm(goto_imm));
  ROM #(.dataWidth(16)) rom_1 (.addr(Instruction), .data(rom_1_data));  // open: sel
  Multiplexer #(.width(8), .enable("false")) multiplexer_1 (
    .in0({8{1'b0}}), .in1(goto_imm), .out(multiplexer_1_out), .sel(Goto_enable));
  _16_register_file u_16_register_file_1 (
    .d(alu_1_output), .Clk(bus_control_1_register_write), .Rd(D), .Clr(Reset), .Ra(A), .Rb(B),
    .a(n16_register_file_1_a), .b(n16_register_file_1_b));
  clock clock_1 (
    .Increment_by(multiplexer_1_out), .Manual_Cycle(Manual_cycle), .Reset(Reset), .Counter(Instruction),
    .State(clock_1_state));
  alu alu_1 (
    .A(n16_register_file_1_a), .B(n16_register_file_1_b), .imm(goto_imm),
    .Op_code(bus_control_1_opcode_to_alu), .in_5(bus_control_1_alu_enable), .\output (alu_1_output));
  bus_control bus_control_1 (
    .Cycle_LSB(clock_1_state[0]), .Cycle_MSB(clock_1_state[1]), .OP(decoder_1_opcode),
    .ALU_Enable(bus_control_1_alu_enable), .Register_Write(bus_control_1_register_write),
    .RAM_Read(bus_control_1_ram_read), .RAM_Write(bus_control_1_ram_write),
    .OPCode_to_ALU(bus_control_1_opcode_to_alu), .Program_Counter_Update(Goto_enable));
  RAM #(.dataWidth(32), .bus("separate")) ram_1 (
    .data(alu_1_output), .str(bus_control_1_ram_write), .ld(bus_control_1_ram_read), .clr(Reset));  // open: addr, din, sel, clk

  // Notes on the sheet:
  //   ROM (Instructions)
  //   contents of rom_1 (hex, n*v repeats v):
  //   f102 1201
  //   Clock
  //   Registers
  //   32-bit CPU
  //   By Cliff, Will, Tom, & Crissy
  //   ALU
  //   Bus Control
  //   RAM
endmodule

module clock (
  input  [7:0] Increment_by,
  input  Manual_Cycle,
  input  Reset,
  output [7:0] Counter,
  output [1:0] State
);

  wire and_1_out, Clock_out, comparator_1_eq, not_1_out;
  wire [7:0] adder_1_out, multiplexer_1_out;

  Clock Clock (.out(Clock_out));
  or or_1 (State[0], Clock_out, Manual_Cycle);
  not not_1 (not_1_out, State[0]);
  Multiplexer #(.width(8), .enable("false")) multiplexer_1 (
    .in0(Increment_by), .in1(8'h1), .out(multiplexer_1_out), .sel(comparator_1_eq));
  Comparator comparator_1 (.a(Increment_by), .b({8{1'b0}}), .eq(comparator_1_eq));  // open: gt, lt
  Register u_Counter (.D(adder_1_out), .Q(Counter), .clk(and_1_out), .clr(Reset));  // open: en
  and and_1 (and_1_out, State[0], State[1]);
  T_Flip_Flop t_ff_1 (.clk(not_1_out), .T(1'b1), .Q(State[1]), .reset(Reset));  // open: Qn, preset, en
  Adder adder_1 (.a(multiplexer_1_out), .b(Counter), .out(adder_1_out));  // open: cin, cout
endmodule

module decoder (
  input  [15:0] Input,
  output [3:0] RegB,
  output [3:0] RegA,
  output [3:0] Destination_register,
  output [3:0] opcode,
  output [3:0] Imm3,
  output [3:0] Imm2,
  output [3:0] Imm1,
  output [7:0] GoTo_Imm
);

  wire [3:0] multiplexer_3_out;
  wire [11:0] demultiplexer_1_out0, demultiplexer_1_out1, demultiplexer_1_out2, demultiplexer_1_out3,
       demultiplexer_1_out4, demultiplexer_1_out5, demultiplexer_1_out6, demultiplexer_1_out7,
       demultiplexer_1_out8, demultiplexer_1_out9, demultiplexer_1_out10, demultiplexer_1_out11,
       demultiplexer_1_out12, demultiplexer_1_out13, demultiplexer_1_out14, demultiplexer_1_out15;

  Demultiplexer #(.select(4), .width(12), .enable("false")) demultiplexer_1 (
    .out0(demultiplexer_1_out0), .out1(demultiplexer_1_out1), .out2(demultiplexer_1_out2),
    .out3(demultiplexer_1_out3), .out4(demultiplexer_1_out4), .out5(demultiplexer_1_out5),
    .out6(demultiplexer_1_out6), .out7(demultiplexer_1_out7), .out8(demultiplexer_1_out8),
    .out9(demultiplexer_1_out9), .out10(demultiplexer_1_out10), .out11(demultiplexer_1_out11),
    .out12(demultiplexer_1_out12), .out13(demultiplexer_1_out13), .out14(demultiplexer_1_out14),
    .out15(demultiplexer_1_out15), .in(Input[11:0]), .sel(Input[15:12]));
  Multiplexer #(.select(4), .width(12), .enable("false")) multiplexer_1 (
    .in0(demultiplexer_1_out0), .in1(demultiplexer_1_out1), .in2(demultiplexer_1_out2),
    .in3(demultiplexer_1_out3), .in4(demultiplexer_1_out4), .in5(demultiplexer_1_out5),
    .in6(demultiplexer_1_out6), .in7(demultiplexer_1_out7), .in8(demultiplexer_1_out8),
    .in9(demultiplexer_1_out9), .out({Destination_register, RegA, RegB}), .sel(Input[15:12]));  // open: in10, in11, in12, in13, in14, in15
  Multiplexer #(.select(4), .width(12), .enable("false")) multiplexer_2 (
    .in10(demultiplexer_1_out10), .in12(demultiplexer_1_out12), .out({Destination_register, Imm1, Imm2}),
    .sel(Input[15:12]));  // open: in0, in1, in2, in3, in4, in5, in6, in7, in8, in9, in11, in13, in14, in15
  Multiplexer #(.select(4), .width(12), .enable("false")) multiplexer_3 (
    .in11(demultiplexer_1_out11), .out({Destination_register, RegA, multiplexer_3_out}), .sel(Input[15:12]));  // open: in0, in1, in2, in3, in4, in5, in6, in7, in8, in9, in10, in12, in13, in14, in15
  Multiplexer #(.select(4), .width(12), .enable("false")) multiplexer_4 (
    .in13(demultiplexer_1_out13), .out({Imm1, Imm2, Imm3}), .sel(Input[15:12]));  // open: in0, in1, in2, in3, in4, in5, in6, in7, in8, in9, in10, in11, in12, in14, in15
  Multiplexer #(.select(4), .width(12), .enable("false")) multiplexer_5 (
    .in14(demultiplexer_1_out14), .out({RegA, GoTo_Imm}), .sel(Input[15:12]));  // open: in0, in1, in2, in3, in4, in5, in6, in7, in8, in9, in10, in11, in12, in13, in15
  Multiplexer #(.select(4), .width(12), .enable("false")) multiplexer_6 (
    .in15(demultiplexer_1_out15), .out({Destination_register, GoTo_Imm}), .sel(Input[15:12]));  // open: in0, in1, in2, in3, in4, in5, in6, in7, in8, in9, in10, in11, in12, in13, in14

  assign opcode = Input[15:12];

  // Other names for the same wires on the sheet: A[3:0] = RegA
endmodule

module _16_register_file (
  input  [31:0] d,
  input  Clk,
  input  [3:0] Rd,
  input  Clr,
  input  [3:0] Ra,
  input  [3:0] Rb,
  output [31:0] a,
  output [31:0] b
);

  wire demultiplexer_1_out0, demultiplexer_1_out1, demultiplexer_1_out2, demultiplexer_1_out3;
  wire [31:0] n3_register_file_1_a, n3_register_file_1_b, n4_register_file_1_a, n4_register_file_1_b,
       n4_register_file_2_a, n4_register_file_2_b, n4_register_file_3_a, n4_register_file_3_b;

  Demultiplexer #(.select(2), .enable("false")) demultiplexer_1 (
    .out0(demultiplexer_1_out0), .out1(demultiplexer_1_out1), .out2(demultiplexer_1_out2),
    .out3(demultiplexer_1_out3), .in(Clk), .sel(Rd[3:2]));
  _3_register_file u_3_register_file_1 (
    .d(d), .Ck(demultiplexer_1_out0), .Rd(Rd[1:0]), .Clr(Clr), .Ra(Ra[1:0]), .Rb(Rb[1:0]),
    .a(n3_register_file_1_a), .b(n3_register_file_1_b));
  _4_register_file u_4_register_file_1 (
    .d(d), .Ck(demultiplexer_1_out1), .Rd(Rd[1:0]), .Clr(Clr), .Ra(Ra[1:0]), .Rb(Rb[1:0]),
    .a(n4_register_file_1_a), .b(n4_register_file_1_b));
  _4_register_file u_4_register_file_2 (
    .d(d), .Ck(demultiplexer_1_out2), .Rd(Rd[1:0]), .Clr(Clr), .Ra(Ra[1:0]), .Rb(Rb[1:0]),
    .a(n4_register_file_2_a), .b(n4_register_file_2_b));
  _4_register_file u_4_register_file_3 (
    .d(d), .Ck(demultiplexer_1_out3), .Rd(Rd[1:0]), .Clr(Clr), .Ra(Ra[1:0]), .Rb(Rb[1:0]),
    .a(n4_register_file_3_a), .b(n4_register_file_3_b));
  Multiplexer #(.select(2), .width(32), .enable("false")) multiplexer_1 (
    .in0(n3_register_file_1_a), .in1(n4_register_file_1_a), .in2(n4_register_file_2_a),
    .in3(n4_register_file_3_a), .out(a), .sel(Ra[3:2]));
  Multiplexer #(.select(2), .width(32), .enable("false")) multiplexer_2 (
    .in0(n3_register_file_1_b), .in1(n4_register_file_1_b), .in2(n4_register_file_2_b),
    .in3(n4_register_file_3_b), .out(b), .sel(Rb[3:2]));

  // Notes on the sheet:
  //   Data in
  //   Write data to register
  //   Note the splitter
  //   Which register?
  //   Reset everything
  //   Select the contents of two registers, Ra Rb
  //   Value of two registers selected
endmodule

module _4_register_file (
  input  [31:0] d,
  input  Ck,
  input  [1:0] Rd,
  input  Clr,
  input  [1:0] Ra,
  input  [1:0] Rb,
  output [31:0] a,
  output [31:0] b
);

  wire demultiplexer_1_out0, demultiplexer_1_out1, demultiplexer_1_out2, demultiplexer_1_out3;
  wire [31:0] register_1_q, register_2_q, register_3_q, register_4_q;

  Demultiplexer #(.select(2), .enable("false")) demultiplexer_1 (
    .out0(demultiplexer_1_out0), .out1(demultiplexer_1_out1), .out2(demultiplexer_1_out2),
    .out3(demultiplexer_1_out3), .in(Ck), .sel(Rd));
  Register #(.width(32)) register_1 (.D(d), .Q(register_1_q), .clk(demultiplexer_1_out0), .clr(Clr));  // open: en
  Register #(.width(32)) register_2 (.D(d), .Q(register_2_q), .clk(demultiplexer_1_out1), .clr(Clr));  // open: en
  Register #(.width(32)) register_3 (.D(d), .Q(register_3_q), .clk(demultiplexer_1_out2), .clr(Clr));  // open: en
  Register #(.width(32)) register_4 (.D(d), .Q(register_4_q), .clk(demultiplexer_1_out3), .clr(Clr));  // open: en
  Multiplexer #(.select(2), .width(32), .enable("false")) multiplexer_1 (
    .in0(register_1_q), .in1(register_2_q), .in2(register_3_q), .in3(register_4_q), .out(a), .sel(Ra));
  Multiplexer #(.select(2), .width(32), .enable("false")) multiplexer_2 (
    .in0(register_1_q), .in1(register_2_q), .in2(register_3_q), .in3(register_4_q), .out(b), .sel(Rb));

  // Notes on the sheet:
  //   Data in
  //   Write signal
  //   Select register to write to
  //   Reset
  //   Registers to select to read from
  //   Values of selected registers
endmodule

module _3_register_file (
  input  [31:0] d,
  input  Ck,
  input  [1:0] Rd,
  input  Clr,
  input  [1:0] Ra,
  input  [1:0] Rb,
  output [31:0] a,
  output [31:0] b
);

  wire demultiplexer_1_out1, demultiplexer_1_out2, demultiplexer_1_out3;
  wire [31:0] register_1_q, register_2_q, register_3_q;

  Demultiplexer #(.select(2), .enable("false")) demultiplexer_1 (
    .out1(demultiplexer_1_out1), .out2(demultiplexer_1_out2), .out3(demultiplexer_1_out3), .in(Ck), .sel(Rd));  // open: out0
  Register #(.width(32)) register_1 (.D(d), .Q(register_1_q), .clk(demultiplexer_1_out1), .clr(Clr));  // open: en
  Register #(.width(32)) register_2 (.D(d), .Q(register_2_q), .clk(demultiplexer_1_out2), .clr(Clr));  // open: en
  Register #(.width(32)) register_3 (.D(d), .Q(register_3_q), .clk(demultiplexer_1_out3), .clr(Clr));  // open: en
  Multiplexer #(.select(2), .width(32), .enable("false")) multiplexer_1 (
    .in0({32{1'b0}}), .in1(register_1_q), .in2(register_2_q), .in3(register_3_q), .out(a), .sel(Ra));
  Multiplexer #(.select(2), .width(32), .enable("false")) multiplexer_2 (
    .in0({32{1'b0}}), .in1(register_1_q), .in2(register_2_q), .in3(register_3_q), .out(b), .sel(Rb));

  // Notes on the sheet:
  //   R0
  //   R1
  //   R2
  //   R3
endmodule

module bus_control (
  input  Cycle_LSB,
  input  Cycle_MSB,
  input  [3:0] OP,
  output ALU_Enable,
  output Register_Write,
  output RAM_Read,
  output RAM_Write,
  output [3:0] OPCode_to_ALU,
  output Program_Counter_Update
);

  wire [3:1] rom_1_data;

  Multiplexer #(.select(4), .width(4), .enable("false")) multiplexer_1 (
    .in0(OP), .in1(OP), .in2(OP), .in3(OP), .in4(OP), .in5(OP), .in6(OP), .in7(OP), .in8(OP), .in9(OP),
    .in12(4'b0000), .in13(4'b0000), .in15(OP), .out(OPCode_to_ALU), .sel(OP));  // open: in10, in11, in14
  ROM #(.addrWidth(6)) rom_1 (
    .addr({OP, Cycle_MSB, Cycle_LSB}),
    .data({ALU_Enable, Register_Write, RAM_Read, RAM_Write, rom_1_data, Program_Counter_Update}));  // open: sel

  // Notes on the sheet:
  //   contents of rom_1 (hex, n*v repeats v):
  //   80 c0 0 0 80 c0 0 0 80 c0 0 0 80 c0 0 0 80 c0 0 0 80 c0 0 0 80 c0 0 0 80 c0 0 0 80 c0 0 0 80 c0 0 0
  //   20 60 0 0 20 60 0 0 80 90 0 0 80 90 0 0 80 81 0 0 80 c0
endmodule

module alu (
  input  [31:0] A,
  input  [31:0] B,
  input  [7:0] imm,
  input  [3:0] Op_code,
  input  in_5,
  output [31:0] \output 
);

  wire comparator_1_eq, comparator_1_gt, comparator_1_lt;
  wire [31:0] adder_1_out, and_1_out, bit_extender_1_out, bit_extender_2_out, bit_extender_3_out,
       bit_extender_4_out, divider_1_out, multiplexer_1_out, multiplier_1_out, or_1_out, subtractor_1_out,
       xnor_1_out;

  assign bit_extender_1_out = {{24{1'b0}}, imm};  // Bit_Extender bit_extender_1
  Adder #(.width(32)) adder_1 (.a(A), .b(B), .out(adder_1_out));  // open: cin, cout
  Subtractor #(.width(32)) subtractor_1 (.a(A), .b(B), .out(subtractor_1_out));  // open: bin, bout
  Multiplier #(.width(32)) multiplier_1 (.a(A), .b(B), .out(multiplier_1_out));  // open: cin, cout
  Divider #(.width(32)) divider_1 (.a(A), .b(B), .out(divider_1_out));  // open: upper, rem
  assign bit_extender_2_out = {{31{1'b0}}, comparator_1_gt};  // Bit_Extender bit_extender_2
  assign bit_extender_3_out = {{31{1'b0}}, comparator_1_eq};  // Bit_Extender bit_extender_3
  Comparator #(.width(32)) comparator_1 (
    .a(A), .b(B), .gt(comparator_1_gt), .eq(comparator_1_eq), .lt(comparator_1_lt));
  assign bit_extender_4_out = {{31{1'b0}}, comparator_1_lt};  // Bit_Extender bit_extender_4
  assign and_1_out = A & B;  // AND_Gate and_1, 32 bits wide
  assign or_1_out = A | B;  // OR_Gate or_1, 32 bits wide
  assign xnor_1_out = ~(A ^ B);  // XNOR_Gate xnor_1, 32 bits wide
  Multiplexer #(.select(4), .width(32), .enable("false")) multiplexer_1 (
    .in0(adder_1_out), .in1(subtractor_1_out), .in2(multiplier_1_out), .in3(divider_1_out),
    .in4(bit_extender_2_out), .in5(bit_extender_3_out), .in6(bit_extender_4_out), .in7(and_1_out),
    .in8(or_1_out), .in9(xnor_1_out), .in10(bit_extender_1_out), .in11(bit_extender_1_out),
    .in12(bit_extender_1_out), .in13(bit_extender_1_out), .in14(bit_extender_1_out),
    .in15(bit_extender_1_out), .out(multiplexer_1_out), .sel(Op_code));
  assign \output  = in_5 ? multiplexer_1_out : 32'bz;  // Controlled_Buffer controlled_buffer_1
endmodule
