// Logisim project Decoder.circ as structural Verilog: 1 circuit, main circuit Decoder
module Decoder (
  input  [15:0] Input,
  output [3:0] Arg2,
  output [3:0] Arg1,
  output [3:0] Destination_register,
  output [3:0] opcode
);


  assign Arg1 = Input[7:4];
  assign Arg2 = Input[3:0];
  assign Destination_register = Input[11:8];
  assign opcode = Input[15:12];
endmodule
