// Logisim project clock.circ as structural Verilog: 1 circuit, main circuit main
module main (
  input  [7:0] Increment_by,
  input  Reset
);

  wire and_1_out, clock_1_out, not_1_out, t_ff_1_q, t_ff_1_qn;
  wire [7:0] adder_1_out, Counter_q, or_1_out;

  Clock clock_1 (.out(clock_1_out));
  not not_1 (not_1_out, clock_1_out);
  T_Flip_Flop t_ff_1 (.clk(not_1_out), .T(1'b1), .Q(t_ff_1_q), .Qn(t_ff_1_qn), .reset(Reset));  // open: preset, en
  assign or_1_out = 8'h1 | Increment_by;  // OR_Gate or_1, 8 bits wide
  Register Counter (.D(adder_1_out), .Q(Counter_q), .clk(and_1_out), .clr(Reset));  // open: en
  and and_1 (and_1_out, clock_1_out, t_ff_1_q);
  Adder adder_1 (.a(or_1_out), .b(Counter_q), .out(adder_1_out));  // open: cin, cout
  RAM ram_1 (.addr(Counter_q));  // open: data, sel, clk, ld, clr
endmodule
